# Fritzing sketch wheelchair_Interface_fritzing (saved by Fritzing 0.9.1b)
breadboards: 1

parts:
  Part1 = Arduino Uno (Rev3)
  Q1 = NPN-Transistor [part_number=2N3904 package="TO92 [THT]"]
  Q2 = NPN-Transistor [part_number=2N3904 package="TO92 [THT]"]
  Q3 = NPN-Transistor [part_number=2N3904 package="TO92 [THT]"]
  Q4 = NPN-Transistor [part_number=2N3904 package="TO92 [THT]"]
  R1 = Resistor [tolerance=±5% resistance=4.7k package=THT]
  R2 = Resistor [tolerance=±5% resistance=4.7k package=THT]
  R3 = Resistor [tolerance=±5% resistance=4.7k package=THT]
  R4 = Resistor [tolerance=±5% resistance=4.7k package=THT]
  R5 = Resistor [tolerance=±5% resistance=4.7k package=THT]
  Q5 = NPN-Transistor [part_number=2N3904 package="TO92 [THT]"]
  X1 = DB9 Connector [package=db9]
  BlueSmirf_Silver = BlueSmirf Silver

nets:
  GND: Part1.GND, Q1.E, Q2.E, Q3.E, Q4.E, Q5.E, X1.8, BlueSmirf_Silver.GND
  N1: Part1.D0/RX, BlueSmirf_Silver.TX_5V
  N2: Part1.D1/TX, BlueSmirf_Silver.RX_5V
  N3: Part1.D2, R1.Pin_0
  N4: Part1.D3_PWM, R2.Pin_0
  N5: Part1.D4, R3.Pin_0
  N6: Part1.D5_PWM, R4.Pin_0
  N7: Part1.D6_PWM, R5.Pin_0
  5V: Part1.5V, BlueSmirf_Silver.VCC
  N8: Part1.VIN, X1.7
  N9: Q1.B, R1.Pin_1
  N10: Q1.C, X1.1
  N11: Q2.B, R2.Pin_1
  N12: Q2.C, X1.2
  N13: Q3.B, R3.Pin_1
  N14: Q3.C, X1.3
  N15: Q4.B, R4.Pin_1
  N16: Q4.C, X1.4
  N17: R5.Pin_1, Q5.B
  N18: Q5.C, X1.6
  N19: BlueSmirf_Silver.RTS_5V, BlueSmirf_Silver.CTS_5V

custom parts:
  DB9 Connector: I used the ribbon cable version, rather than the original PCB mount version available in Fritzing. DB9 Connector Standard DB9 (D-Sub 9) serial connector. Can be used for CAN bus as well as RS485 and RS232. Footprint production proven. Spark Fun Electronics SKU : PRT-00429
  BlueSmirf Silver: I have edited the Bluetooth Mate Silver to match the BlueSmirf Silver that I used. They are similar, but the pin connections are different. Change them accordingly to use a Bluetooth Mate. Description: The Bluetooth Mate is very similar to our BlueSMiRF modem, but it is designed specifically to be used with our Arduino Pros and LilyPad Arduinos. These modems work as a serial (RX/TX) pipe, and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

// code stored in the sketch: Computer-Wheelchair_Interface.ino
/*
 This code is modified from a publicly available example by Tom Igoe, found here:
 
 http://www.arduino.cc/en/Tutorial/SwitchCase2
 
 To control from a remote computer/tablet/phone via Blutetooth, use a terminal
 program like Putty to send any character to the BlueSMiRF module, which should
 be connected to the serial I/O pins of the Arduino.
 The characters a, b, c, d, and e, will turn on digital output pins
 2, 3, 4, 5, and 6, respectively.  Any other character will turn all output pins
 off.  Change the characters and pins as desired.
 
 The circuit:
 * 5 transistors (base pins) attached to Arduino digital pins 2 through 6 through
 4.7 Kilo ohm resistors
 
 (Modified from example code by Gavin Philips)
 */

void setup() {
  // initialize serial communication:
  Serial.begin(115200); 
  // initialize the output pins:
  for (int thisPin = 2; thisPin < 7; thisPin++) {
    pinMode(thisPin, OUTPUT);
  } 
}

void loop() {
  // read the input:
  if (Serial.available() > 0) {
    int inByte = Serial.read();
    // do something different depending on the character received.  
    // The switch statement expects single number values for each case;
    // in this exmaple, though, you're using single quotes to tell
    // the controller to get the ASCII value for the character.  For 
    // example 'a' = 97, 'b' = 98, and so forth:

    switch (inByte) {
    case 'a':    
      digitalWrite(2, HIGH);
      break;
    case 'b':    
      digitalWrite(3, HIGH);
      break;
    case 'c':    
      digitalWrite(4, HIGH);
      break;
    case 'd':    
      digitalWrite(5, HIGH);
      break;
    case 'e':    
      digitalWrite(6, HIGH);
      break;
    default:
      // turn all the outputs off:
      for (int thisPin = 2; thisPin < 7; thisPin++) {
        digitalWrite(thisPin, LOW);
      }
    } 
  }
}
